# Fritzing sketch wiring (saved by Fritzing 0.9.2b)

parts:
  Part1 = Arduino Ethernet Shield (Rev3)
  R1 = Resistor [tolerance=±5% resistance=10k package=THT]
  DHT11 = DHT11 Humitidy and Temperature Sensor
  S1 = SWITCH-MOMENTARY-2 [package=tactile-switch-1101ne]
  S2 = SWITCH-MOMENTARY-2 [package=tactile-switch-1101ne]
  R2 = Resistor [tolerance=±5% resistance=10k package=THT]

nets:
  5V: Part1.5V, R1.Pin_1, DHT11.VDD, S1.2, S2.2
  GND: Part1.GND, DHT11.GND, R2.Pin_1
  N1: Part1.D2, R1.Pin_0, DHT11.DATA
  N2: Part1.PWM_D3, S1.1, S2.1, R2.Pin_0

custom parts:
  DHT11 Humitidy and Temperature Sensor: DHT11 Humidity and Temperature Sensor
